# Fritzing sketch DiscoLed (saved by Fritzing 0.6.4b)
breadboards: 1

parts:
  Arduino1 = Arduino
  LED1 = RGB LED (com. anode, rbg) [package="5 mm [THT]"]
  R2 = Resistor [tolerance=±5% resistance=220 package=THT]
  R3 = Resistor [tolerance=±5% resistance=220 package=THT]
  R4 = Resistor [tolerance=±5% resistance=220 package=THT]

nets:
  N1: Arduino1.GND, LED1.common_anode
  N2: Arduino1.D6, R3.Pin_0
  N3: Arduino1.D5, R4.Pin_0
  N4: Arduino1.D3, R2.Pin_0
  N5: LED1.red_cathode, R2.Pin_1
  N6: LED1.blue_cathode, R3.Pin_1
  N7: LED1.green_cathode, R4.Pin_1
