# Fritzing sketch Espanta Espiritos (saved by Fritzing 0.6.4b)
breadboards: 1

parts:
  Arduino1 = Arduino
  R1 = Resistor [tolerance=±5% resistance=10k package=THT]
  R2 = Resistor [tolerance=±5% resistance=10k package=THT]
  R3 = Resistor [tolerance=±5% resistance=10k package=THT]
  J1 = Piezo Speaker

nets:
  N1: Arduino1.D8, Arduino1.D7, Arduino1.D4, Arduino1.GND, R1.Pin_1, R2.Pin_1, R3.Pin_1, J1.pin1
  N2: Arduino1.D2, J1.pin2

notes:
  COIN 1 SET 1
  COIN 1 SET 2
  COIN 1 SET 3
  COIN 2 SET 2
  COIN 2 SET 1
  COIN 2 SET 3
  resistors 10k Ohm -+5%
