# Fritzing sketch Motor (saved by Fritzing 0.6.4b)
breadboards: 1

parts:
  MUX = L293D [package=THT]
  Arduino = Arduino
  Motor = DC Motor

nets:
  N1: MUX.Enable_1, MUX.In_1, Arduino.D12, Arduino.D7
  N2: MUX.Out_1_(_Controlled_by_Enable_1_), Motor.pin_1
  N3: MUX.0V, MUX.Out_3_(_Controlled_by_Enable_2_), MUX.Out_4_(_Controlled_by_Enable_2_), Arduino.GND
  N4: MUX.Out_2_(_Controlled_by_Enable_1_), Motor.pin_2
  N5: MUX.In_2, Arduino.D8
  N6: MUX.+Vmotor, MUX.+V, Arduino.+5V
