# Fritzing sketch SimpleButton (saved by Fritzing 0.6.4b)
breadboards: 1

parts:
  Arduino1 = Arduino
  LED1 = LED - 5mm [color="Red (633nm)" package="5 mm [THT]"]
  R1 = Resistor [tolerance=±5% resistance=220 package=THT]
  S1 = Pushbutton [package="[THT]"]

nets:
  N1: Arduino1.GND, R1.Pin_1, S1.Pin_1, S1.Pin_2
  N2: Arduino1.D13, Arduino1.D4, LED1.cathode, S1.Pin_3, S1.Pin_4
  N3: LED1.anode, R1.Pin_0
